# Fritzing sketch pcb (saved by Fritzing 0.9.3b)
circuit board: 15.24cm x 15.24cm
breadboards: 1

parts:
  part = Analog Digital MUX Breakout
  part_2 = Header 5x2 [package=avr_icsp]
  part_3 = male pin header, 10 pins [form="♂ (male)"]
  part_4 = male pin header, 10 pins [form="♂ (male)"]
  part_5 = Analog Digital MUX Breakout
  part_6 = Header 5x2 [package=avr_icsp]
  part_7 = male pin header, 10 pins [form="♂ (male)"]
  part_8 = male pin header, 10 pins [form="♂ (male)"]
  part_9 = Analog Digital MUX Breakout
  part_10 = Header 5x2 [package=avr_icsp]
  part_11 = male pin header, 10 pins [form="♂ (male)"]
  part_12 = male pin header, 10 pins [form="♂ (male)"]
  part_13 = Analog Digital MUX Breakout
  part_14 = Header 5x2 [package=avr_icsp]
  part_15 = male pin header, 10 pins [form="♂ (male)"]
  part_16 = male pin header, 10 pins [form="♂ (male)"]
  part_17 = SparkFun Pro Micro
  part_18 = Header 5x2 [package=avr_icsp]

nets:
  N1: part.GND, part_2.1, part_3.pin1, part_3.pin2, part_3.pin3, part_3.pin4, part_3.pin5, part_3.pin6, part_3.pin7, part_3.pin8, part_3.pin9, part_3.pin10
  N2: part.VCC, part_2.2, part_4.pin1, part_4.pin2, part_4.pin3, part_4.pin4, part_4.pin5, part_4.pin6, part_4.pin7, part_4.pin8, part_4.pin9, part_4.pin10
  N3: part.S0, part_2.4
  N4: part.S1, part_2.6
  N5: part.S2, part_2.8
  N6: part.S3, part_2.10
  N7: part.SIG, part_2.3
  N8: part_5.GND, part_6.1, part_7.pin1, part_7.pin2, part_7.pin3, part_7.pin4, part_7.pin5, part_7.pin6, part_7.pin7, part_7.pin8, part_7.pin9, part_7.pin10
  N9: part_5.VCC, part_6.2, part_8.pin1, part_8.pin2, part_8.pin3, part_8.pin4, part_8.pin5, part_8.pin6, part_8.pin7, part_8.pin8, part_8.pin9, part_8.pin10
  N10: part_5.S0, part_6.4
  N11: part_5.S1, part_6.6
  N12: part_5.S2, part_6.8
  N13: part_5.S3, part_6.10
  N14: part_5.SIG, part_6.5
  N15: part_9.GND, part_10.1, part_11.pin1, part_11.pin2, part_11.pin3, part_11.pin4, part_11.pin5, part_11.pin6, part_11.pin7, part_11.pin8, part_11.pin9, part_11.pin10
  N16: part_9.VCC, part_10.2, part_12.pin1, part_12.pin2, part_12.pin3, part_12.pin4, part_12.pin5, part_12.pin6, part_12.pin7, part_12.pin8, part_12.pin9, part_12.pin10
  N17: part_9.S0, part_10.4
  N18: part_9.S1, part_10.6
  N19: part_9.S2, part_10.8
  N20: part_9.S3, part_10.10
  N21: part_9.SIG, part_10.7
  N22: part_13.GND, part_14.1, part_15.pin1, part_15.pin2, part_15.pin3, part_15.pin4, part_15.pin5, part_15.pin6, part_15.pin7, part_15.pin8, part_15.pin9, part_15.pin10
  N23: part_13.VCC, part_14.2, part_16.pin1, part_16.pin2, part_16.pin3, part_16.pin4, part_16.pin5, part_16.pin6, part_16.pin7, part_16.pin8, part_16.pin9, part_16.pin10
  N24: part_13.S0, part_14.4
  N25: part_13.S1, part_14.6
  N26: part_13.S2, part_14.8
  N27: part_13.S3, part_14.10
  N28: part_13.SIG, part_14.9
  N29: part_17.GND, part_18.1
  N30: part_17.10, part_18.10
  N31: part_17.16, part_18.8
  N32: part_17.14, part_18.6
  N33: part_17.15, part_18.4
  N34: part_17.A0, part_18.9
  N35: part_17.A1, part_18.7
  N36: part_17.A2, part_18.5
  N37: part_17.A3, part_18.3
  N38: part_17.VCC, part_18.2

custom parts:
  SparkFun Pro Micro: The Pro Micro is similar to the Pro Mini except with an ATmega32U4 on board. The USB transceiver inside the 32U4 allows us to add USB connectivity on-board and do away with bulky external USB interface. Based on: https://github.com/unorthodox-engineers/unorthodox-arduino/blob/master/Unorthodox/fritzing/parts/Pro%20Micro.fzpz
